# Fritzing sketch mcp4922_for_arduino (saved by Fritzing 0.6.3b)
breadboards: 1

parts:
  IC1 = IC, DIP package, 14 pins [chip_label=IC spacing=300mil]
  Arduino1 = Arduino
  C1 = Ceramic Capacitor [capacitance=100nF voltage=50V package="100 mil [THT, multilayer]"]
  C2 = Ceramic Capacitor [capacitance=100nF voltage=50V package="100 mil [THT, multilayer]"]
  R1 = Resistor [tolerance=±5% resistance=100k package=THT]
  J1 = female pin header, 2 pins [form="♂ (male)"]

nets:
  N1: IC1.pin1, IC1.pin9, Arduino1.+5V, C1.1, R1.Pin_1
  N2: IC1.pin3, Arduino1.D9
  N3: IC1.pin4, Arduino1.D13
  N4: IC1.pin5, Arduino1.D11
  N5: IC1.pin8, Arduino1.D8
  N6: IC1.pin10, J1.pin2
  N7: IC1.pin11, IC1.pin13, C2.0, R1.Pin_0
  N8: IC1.pin12, Arduino1.GND, C1.0, C2.1
  N9: IC1.pin14, J1.pin1

notes:
  Output A, Output B
